// Logisim project P2.2.2.circ as structural Verilog: 1 circuit, main circuit main
module main (
  input  [1:0] in_1
);

  wire multiplexer_1_out, multiplexer_2_out;

  Multiplexer #(.select(2), .enable("false")) multiplexer_1 (
    .in0(1'b0), .in1(1'b1), .in2(1'b1), .in3(1'b0), .out(multiplexer_1_out), .sel(in_1));
  Multiplexer #(.select(2), .enable("false")) multiplexer_2 (
    .in0(1'b0), .in1(1'b0), .in2(1'b0), .in3(1'b1), .out(multiplexer_2_out), .sel(in_1));
  LED led_1 (.in(multiplexer_1_out));
  LED led_2 (.in(multiplexer_2_out));

  // Notes on the sheet:
  //   HALF ADDER USANDO MUX 4:1
  //   SUM
  //   CARRY
endmodule
