// Logisim project P2.2.circ as structural Verilog: 1 circuit, main circuit main
module main (
  input  in_1,
  input  [1:0] in_2
);

  wire multiplexer_1_out, multiplexer_2_out, not_1_out;

  not not_1 (not_1_out, in_1);
  Multiplexer #(.select(2), .enable("false")) multiplexer_1 (
    .in0(in_1), .in1(not_1_out), .in2(not_1_out), .in3(in_1), .out(multiplexer_1_out), .sel(in_2));
  Multiplexer #(.select(2), .enable("false")) multiplexer_2 (
    .in0(1'b0), .in1(in_1), .in2(in_1), .in3(1'b1), .out(multiplexer_2_out), .sel(in_2));
  LED led_1 (.in(multiplexer_1_out));
  LED led_2 (.in(multiplexer_2_out));

  // Notes on the sheet:
  //   Full Adder con MUx 4:1
  //   SUM
  //   CARRY
endmodule
