// Logisim project EsquemaBCD.circ as structural Verilog: 1 circuit, main circuit main
module main (
  input  x,
  input  y,
  input  z,
  output a,
  output b,
  output c,
  output d,
  output e,
  output f,
  output g
);

  wire and_1_out, and_2_out, and_3_out, and_4_out, and_5_out, and_6_out, not_1_out, not_2_out, not_3_out,
       not_4_out, not_5_out, not_6_out, not_7_out, not_8_out;

  not not_1 (not_1_out, x);
  not not_2 (not_2_out, y);
  not not_3 (not_3_out, x);
  not not_4 (not_4_out, x);
  not not_5 (not_5_out, y);
  not not_6 (not_6_out, x);
  not not_7 (not_7_out, x);
  not not_8 (not_8_out, z);
  not not_9 (g, y);
  and and_1 (and_1_out, not_1_out, not_2_out);
  and and_2 (and_2_out, not_3_out, z);
  and and_3 (and_3_out, not_4_out, not_5_out);
  and and_4 (and_4_out, not_6_out, z);
  and and_5 (and_5_out, not_7_out, z);
  and and_6 (and_6_out, x, not_8_out);
  or or_1 (b, and_1_out, and_1_out, and_2_out);
  or or_2 (c, and_3_out, and_4_out);
  or or_3 (d, and_5_out, y, and_6_out, and_6_out);
  _7_Segment_Display u_7_segment_display_1 (.g(g), .f(1'b1), .a(1'b1), .b(b), .e(1'b1), .d(d), .c(c));  // open: dp

  assign a = 1'b1;
  assign e = 1'b1;
  assign f = 1'b1;
endmodule
