// Logisim project RetoPrimerParcial.circ as structural Verilog: 1 circuit, main circuit main
module main (
  input  S_R,
  input  in_2,
  input  A6,
  input  A4,
  input  A5,
  input  A3,
  input  A2,
  input  A1,
  input  A0,
  input  B7,
  input  B6,
  input  B4,
  input  B3,
  input  B2,
  input  B1,
  input  B5,
  input  B0
);

  wire and_1_out, and_2_out, and_3_out, and_4_out, and_5_out, and_6_out, and_7_out, and_8_out, and_9_out,
       and_10_out, and_11_out, and_12_out, and_13_out, and_14_out, and_15_out, and_16_out, and_17_out,
       and_18_out, and_19_out, and_20_out, and_21_out, and_22_out, and_23_out, and_24_out, or_1_out,
       or_8_out, xor_1_out, xor_2_out, xor_3_out, xor_4_out, xor_5_out, xor_6_out, xor_7_out, xor_8_out,
       xor_9_out, xor_10_out, xor_11_out, xor_12_out, xor_13_out, xor_14_out, xor_15_out, xor_16_out,
       xor_17_out, xor_18_out, xor_19_out, xor_20_out, xor_21_out, xor_22_out, xor_23_out, xor_24_out,
       xor_25_out;

  and and_1 (and_1_out, B7, xor_1_out);
  LED led_1 (.in(xor_3_out));
  and and_2 (and_2_out, B7, B7);
  or or_1 (or_1_out, and_1_out, and_2_out, and_3_out);
  LED led_2 (.in(or_1_out));
  xor xor_1 (xor_1_out, in_2, S_R);
  xor xor_2 (xor_2_out, xor_1_out, B7);
  and and_3 (and_3_out, B7, B7);
  xor xor_3 (xor_3_out, or_1_out, B7);
  xor xor_4 (xor_4_out, B7, xor_2_out);
  LED led_3 (.in(xor_4_out));
  and and_4 (and_4_out, B6, xor_5_out);
  and and_5 (and_5_out, B6, B6);
  or or_2 (B7, and_4_out, and_5_out, and_6_out);
  xor xor_5 (xor_5_out, A6, S_R);
  xor xor_6 (xor_6_out, xor_5_out, B6);
  and and_6 (and_6_out, B6, B6);
  xor xor_7 (xor_7_out, B6, xor_6_out);
  LED led_4 (.in(xor_7_out));
  and and_7 (and_7_out, B5, xor_8_out);
  and and_8 (and_8_out, B5, B5);
  or or_3 (B6, and_7_out, and_8_out, and_9_out);
  xor xor_8 (xor_8_out, A5, S_R);
  and and_9 (and_9_out, B5, B5);
  xor xor_9 (xor_9_out, xor_8_out, B5);
  and and_10 (and_10_out, B4, xor_11_out);
  xor xor_10 (xor_10_out, B5, xor_9_out);
  LED led_5 (.in(xor_10_out));
  and and_11 (and_11_out, B4, B4);
  or or_4 (B5, and_10_out, and_11_out, and_12_out);
  xor xor_11 (xor_11_out, A4, S_R);
  xor xor_12 (xor_12_out, xor_11_out, B4);
  and and_12 (and_12_out, B4, B4);
  xor xor_13 (xor_13_out, B4, xor_12_out);
  LED led_6 (.in(xor_13_out));
  and and_13 (and_13_out, B3, xor_14_out);
  and and_14 (and_14_out, B3, B3);
  or or_5 (B4, and_13_out, and_14_out, and_15_out);
  xor xor_14 (xor_14_out, A3, S_R);
  and and_15 (and_15_out, B3, B3);
  xor xor_15 (xor_15_out, xor_14_out, B3);
  xor xor_16 (xor_16_out, B3, xor_15_out);
  LED led_7 (.in(xor_16_out));
  and and_16 (and_16_out, B2, xor_17_out);
  and and_17 (and_17_out, B2, B2);
  or or_6 (B3, and_16_out, and_17_out, and_18_out);
  xor xor_17 (xor_17_out, A2, S_R);
  xor xor_18 (xor_18_out, xor_17_out, B2);
  and and_18 (and_18_out, B2, B2);
  xor xor_19 (xor_19_out, B2, xor_18_out);
  LED led_8 (.in(xor_19_out));
  and and_19 (and_19_out, B1, xor_20_out);
  and and_20 (and_20_out, or_8_out, B1);
  or or_7 (B2, and_19_out, and_20_out, and_21_out);
  xor xor_20 (xor_20_out, A1, S_R);
  and and_21 (and_21_out, or_8_out, B1);
  xor xor_21 (xor_21_out, xor_20_out, B1);
  xor xor_22 (xor_22_out, or_8_out, xor_21_out);
  and and_22 (and_22_out, B0, xor_23_out);
  LED led_9 (.in(xor_22_out));
  and and_23 (and_23_out, S_R, B0);
  or or_8 (or_8_out, and_22_out, and_23_out, and_24_out);
  and and_24 (and_24_out, S_R, B0);
  xor xor_23 (xor_23_out, A0, S_R);
  xor xor_24 (xor_24_out, xor_23_out, B0);
  xor xor_25 (xor_25_out, S_R, xor_24_out);
  LED led_10 (.in(xor_25_out));

  // Notes on the sheet:
  //   OV
  //   C
  //   A7
  //   S7
  //   S6
  //   S5
  //   S4
  //   S3
  //   S2
  //   S1
  //   S0
endmodule
